// Digital circuit 1bitadder.dig as structural Verilog
module _1bitadder (
  input  A,
  input  B,
  input  CIN,
  output SUM,
  output cout
);

  wire and_1_out, and_2_out, xor_1_out;

  xor xor_1 (xor_1_out, A, B);
  and and_1 (and_1_out, A, B);
  and and_2 (and_2_out, xor_1_out, CIN);
  xor xor_2 (SUM, xor_1_out, CIN);
  or or_1 (cout, and_1_out, and_2_out);
endmodule
